# Fritzing sketch Sumo_Sketch1 (saved by Fritzing 0.9.5d)
breadboards: 1

parts:
  Pico_H1 = Raspberry Pi Pico H
  hc-sr1 = hc-sr04
  M1 = DC Motor
  M2 = DC Motor
  S1 = H-Bridge with L298N
  VCC1 = Battery block 9V
  J2 = Basic Servo
  J3 = Basic Servo

nets:
  GND: Pico_H1.GND, hc-sr1.GND, S1.GND, VCC1.-, J2.gnd, J3.gnd
  3V3: Pico_H1.3V3, hc-sr1.VCC
  N1: Pico_H1.GP22, hc-sr1.Trig
  N2: Pico_H1.GP21, hc-sr1.Echo
  N3: Pico_H1.GP8, S1.ENB
  N4: Pico_H1.GP7, S1.IN4
  N5: Pico_H1.GP6, S1.IN3
  N6: Pico_H1.GP4, S1.ENA
  N7: Pico_H1.GP3, S1.IN1
  N8: Pico_H1.GP2, S1.IN2
  N9: M1.pin_1, S1.M1-02
  N10: M1.pin_2, S1.M1-01
  N11: M2.pin_1, S1.M2-02
  N12: M2.pin_2, S1.M2-01
  N13: S1.5V, VCC1.+
  VCC: J2.vcc, J3.vcc
  N14: J2.pulse, J3.pulse

custom parts:
  Raspberry Pi Pico H: Raspberry Pi Pico H. Based around the RP2040 microcontroller the Pico H is a low cost microcontroller device bringing Raspberry Pi quality, cost, and easy of use to the microcontroller space.
  H-Bridge with L298N: h-bridge
